# Fritzing sketch circuito1 (saved by Fritzing 0.9.2b)
breadboards: 1

parts:
  Componente1 = Arduino Nano (Rev3.0)
  J1 = Basic Servo
  S1 = Pushbutton [package="[SMD]"]
  R1 = Resistor [tolerance=±5% resistance=10k package="0805 [SMD]"]

nets:
  N1: Componente1.D2, S1.Pin_1, S1.Pin_2, R1.Pin_0
  N2: Componente1.D9, J1.pulse
  VIN: Componente1.VIN, J1.vcc, S1.Pin_3, S1.Pin_4
  N3: J1.gnd, R1.Pin_1

notes:
  https://www.arduino.cc/en/Tutorial/Button
  https://www.arduino.cc/en/Tutorial/Sweep
